// Logisim project 7seg.circ as structural Verilog: 1 circuit, main circuit main
module main (
  input  A,
  input  B,
  input  Vcc,
  input  GND
);

  wire and_1_out, and_2_out, and_3_out, and_4_out, not_1_out, not_2_out, not_3_out, not_4_out, or_1_out,
       or_2_out, or_3_out, or_4_out;

  not not_1 (not_1_out, B);
  not not_2 (not_2_out, A);
  not not_3 (not_3_out, A);
  not not_4 (not_4_out, B);
  and and_1 (and_1_out, A, B);
  and and_2 (and_2_out, A, not_1_out);
  and and_3 (and_3_out, not_2_out, B);
  and and_4 (and_4_out, not_3_out, not_4_out);
  or or_1 (or_1_out, and_4_out, and_2_out, and_1_out);
  or or_2 (or_2_out, and_4_out, and_1_out, and_3_out);
  or or_3 (or_3_out, and_2_out, and_4_out);
  or or_4 (or_4_out, and_1_out, and_2_out);
  _7_Segment_Display u_7_segment_display_1 (
    .g(or_4_out), .f(and_4_out), .a(or_1_out), .b(Vcc), .e(or_3_out), .d(or_1_out), .c(or_2_out), .dp(GND));
endmodule
