// Logisim project quiz1.circ as structural Verilog: 1 circuit, main circuit main
module main (
  input  A,
  input  B,
  input  C,
  output out_4
);

  wire and_1_out, and_2_out, and_3_out, nor_1_out, or_1_out;

  or or_1 (or_1_out, C, B);
  nor nor_1 (nor_1_out, C, B);
  and and_1 (and_1_out, or_1_out, A);
  and and_2 (and_2_out, nor_1_out, C);
  and and_3 (and_3_out, C, B, A);
  or or_2 (out_4, and_1_out, and_2_out, and_3_out);
endmodule
