// Logisim project quiz2.circ as structural Verilog: 1 circuit, main circuit main
module main (
  input  A,
  input  B,
  input  C,
  output X,
  output Y
);

  wire and_1_out, and_2_out, not_1_out, not_2_out;

  not not_1 (not_1_out, B);
  not not_2 (not_2_out, C);
  and and_1 (and_1_out, A, not_1_out, C);
  and and_2 (and_2_out, A, B, not_2_out);
  and and_3 (Y, A, B, C);
  or or_1 (X, and_1_out, and_2_out, Y);
endmodule
