// Logisim project Quiz2.6.circ as structural Verilog: 2 circuits, main circuit main
module main (
);

  Clock clock_1 ();  // open: out
endmodule

module fsm (
  input  i,
  output Q
);

  wire and_1_out, and_2_out, clock_1_out, d_ff_1_q, not_1_out, not_2_out;

  Clock clock_1 (.out(clock_1_out));
  D_Flip_Flop d_ff_1 (.D(Q), .clk(clock_1_out), .Q(d_ff_1_q));  // open: Qn, preset, reset
  not not_1 (not_1_out, i);
  not not_2 (not_2_out, d_ff_1_q);
  and and_1 (and_1_out, not_1_out, d_ff_1_q);
  or or_1 (Q, and_1_out, and_2_out);
  and and_2 (and_2_out, i, not_2_out);
endmodule
