// Logisim project Quiz2.7.circ as structural Verilog: 2 circuits, main circuit main
module main (
  input  in_1,
  output [1:0] out_2
);

  wire clock_1_out;
  wire [1:0] d_ff_1_q;

  D_Flip_Flop d_ff_1 (.D(out_2[0]), .clk(clock_1_out), .Q(d_ff_1_q[0]));  // open: Qn, preset, reset
  D_Flip_Flop d_ff_2 (.D(out_2[1]), .clk(clock_1_out), .Q(d_ff_1_q[1]));  // open: Qn, preset, reset
  Clock clock_1 (.out(clock_1_out));
  counter counter_1 (.Q(d_ff_1_q), .CLK(in_1), .Qn(out_2));
endmodule

module counter (
  input  [1:0] Q,
  input  CLK,
  output [1:0] Qn
);

  wire and_1_out, and_2_out, and_3_out, and_4_out, and_5_out, not_1_out, not_2_out, not_3_out;

  not not_1 (not_1_out, Q[1]);
  not not_2 (not_2_out, Q[0]);
  not not_3 (not_3_out, CLK);
  and and_1 (and_1_out, not_1_out, Q[0], CLK);
  and and_2 (and_2_out, Q[1], not_2_out);
  and and_3 (and_3_out, Q[1], not_3_out);
  and and_4 (and_4_out, not_2_out, CLK);
  and and_5 (and_5_out, Q[0], not_3_out);
  or or_1 (Qn[1], and_1_out, and_2_out, and_3_out);
  or or_2 (Qn[0], and_4_out, and_5_out);
endmodule
